# Fritzing sketch rpi_digital_camera (saved by Fritzing 0.9.3b)
breadboards: 1

parts:
  Raspberry_Pi_1 = Raspberry Pi 3 [part_number=RPI-3-V1.2]
  LED1 = LEDs [package=led10mm]
  Switch1 = Momentary Switch [package=ksa_sealed_tac_switch]
  R1 = Resistor [tolerance=±5% resistance=330 package="2512 [SMD]"]

nets:
  N1: Raspberry_Pi_1.GPIO23, R1.Pin_1
  N2: Raspberry_Pi_1.GND, LED1.C, Switch1.4
  N3: Raspberry_Pi_1.GPIO18, Switch1.2
  N4: LED1.A, R1.Pin_0
